// Logisim project karnaugh.circ as structural Verilog: 1 circuit, main circuit main
module main (
  input  A,
  input  B,
  input  A1,
  input  B1,
  input  A2,
  input  B2,
  input  A3,
  input  B3,
  input  A4,
  input  B4,
  input  A5,
  output out_12,
  output out_13,
  output out_14,
  output out_15,
  output out_16,
  output out_17
);

  wire and_1_out, and_3_out, and_4_out, not_1_out, not_2_out, not_3_out, not_4_out, not_5_out, not_6_out,
       not_10_out, or_1_out, or_3_out, or_4_out;

  not not_1 (not_1_out, A1);
  not not_2 (not_2_out, B1);
  and and_1 (and_1_out, A2, B2);
  not not_3 (not_3_out, A3);
  not not_4 (not_4_out, B3);
  not not_5 (not_5_out, A4);
  not not_6 (not_6_out, B4);
  not not_7 (out_17, A5);
  or or_1 (or_1_out, A, B);
  and and_2 (out_13, not_1_out, not_2_out);
  not not_8 (out_14, and_1_out);
  or or_2 (out_15, not_3_out, not_4_out);
  and and_3 (and_3_out, A4, B4);
  or or_3 (or_3_out, not_5_out, B4);
  not not_9 (out_12, or_1_out);
  not not_10 (not_10_out, and_3_out);
  or or_4 (or_4_out, B4, not_6_out);
  and and_4 (and_4_out, not_10_out, or_3_out);
  and and_5 (out_16, and_4_out, or_4_out);

  // Notes on the sheet:
  //   -(A + B)
  //   -A * -B
  //   -(A * B)
  //   -A + -B
endmodule
