// Logisim project logic_bloc.circ as structural Verilog: 1 circuit, main circuit main
module main (
  input  A,
  input  B,
  input  C,
  output D
);

  wire and_1_out, and_2_out, and_3_out, and_4_out, and_5_out, not_1_out, not_2_out, or_1_out, or_2_out;

  and and_1 (and_1_out, A, C);
  and and_2 (and_2_out, B, not_1_out);
  not not_1 (not_1_out, C);
  not not_2 (not_2_out, A);
  and and_3 (and_3_out, not_2_out, and_2_out);
  and and_4 (and_4_out, B, C);
  and and_5 (and_5_out, A, B);
  or or_1 (or_1_out, and_1_out, and_3_out);
  or or_2 (or_2_out, and_5_out, and_4_out);
  or or_3 (D, or_1_out, or_2_out);
endmodule
