// Logisim project madness.circ as structural Verilog: 1 circuit, main circuit main
module main (
  input  A,
  input  B,
  input  C,
  input  in_4,
  input  in_5,
  input  in_6,
  output out_7,
  output out_8
);

  wire and_1_out, and_2_out, and_3_out, not_1_out, not_2_out, or_1_out, or_2_out;

  not not_1 (not_1_out, B);
  and and_1 (and_1_out, A, not_1_out);
  and and_2 (and_2_out, B, C);
  and and_3 (and_3_out, and_1_out, and_2_out);
  not not_2 (not_2_out, and_3_out);
  or or_1 (or_1_out, and_1_out, not_2_out);
  or or_2 (or_2_out, not_2_out, and_2_out);
  and and_4 (out_7, or_1_out, or_2_out);

  assign out_8 = 1'b1;
  // also tied to GND on the sheet: {in_4, in_5, in_6}
endmodule
