// Logisim project multiplexor.circ as structural Verilog: 1 circuit, main circuit main
module main (
  input  A,
  input  B,
  input  S,
  output out_4
);

  wire and_1_out, and_2_out, not_1_out, Sel0_out, Sel1_out;

  and Sel0 (Sel0_out, A, B);
  or Sel1 (Sel1_out, A, B);
  not not_1 (not_1_out, S);
  and and_1 (and_1_out, Sel0_out, not_1_out);
  and and_2 (and_2_out, S, Sel1_out);
  or or_1 (out_4, and_1_out, and_2_out);
endmodule
