// Logisim project plexer.circ as structural Verilog: 1 circuit, main circuit main
module main (
  input  [2:0] in_1,
  input  A,
  input  B,
  input  S,
  output out_5,
  output out_6,
  output out_7,
  output out_8,
  output out_9,
  output out_10,
  output out_11,
  output out_12,
  output out_13,
  output out_14
);

  wire and_1_out, and_2_out, not_1_out;

  not not_1 (not_1_out, S);
  Decoder #(.select(3)) decoder_1 (
    .out0(out_5), .out1(out_6), .out2(out_7), .out3(out_8), .out4(out_9), .out5(out_10), .out6(out_11),
    .out7(out_12), .sel(in_1));  // open: en
  and and_1 (and_1_out, A, not_1_out);
  and and_2 (and_2_out, S, B);
  or or_1 (out_13, and_1_out, and_2_out);
  Multiplexer #(.enable("false")) multiplexer_1 (.in0(A), .in1(B), .out(out_14), .sel(S));
endmodule
